# Fritzing sketch Projeto em Fritzing (saved by Fritzing 1.0.4)
breadboards: 1

parts:
  RHT1 = Humidity and Temperature Sensor RHT03
  U1 = LuaNode32 / ESP32 [part_number=ESP32S-PIN30]
  R1 = Resistor [tolerance=±5% power=0.25W resistance=220 package=THT]
  Q1 = Basic FET N-Channel [package="D2Pak [SMD]"]
  M2 = seeed grove atomizer v1.0
  BAT1 = LIPO-2000mAh [package=lipo-2000]

nets:
  VCC: RHT1.Vcc, U1.3V3
  N1: RHT1.Data-signal, U1.D15
  N2: RHT1.GND_2, U1.GND, Q1.source, BAT1.-
  N3: U1.D25, R1.Pin_0
  VIN: U1.Vin, M2.VCC, BAT1.+
  N4: R1.Pin_1, Q1.Gate
  N5: Q1.drain, M2.GND

custom parts:
  LuaNode32 / ESP32: New Image for LuaNode32 DOIT ESP32 DEVKIT V1. Base parts from LuaNode32 / ESP32 ESP32 based LuaNode32 by G.Noorlander DOIT Esp32 DevKit v1 (30 pins long, 11 pins width) by Werner Rothschopf (modified by vanepp Dec 2018)
  seeed grove atomizer v1.0: Grove - Water Atomization is a perfect module for you to quickly DIY a humidifier with Arduino. You can also develop more advanced and interesting projects with digital scent technology and any other situations in which atomization required.

// code stored in the sketch: Projeto.ino
#include <DHT.h>

// ===================================
// CONFIGURAÇÕES DO PROJETO
// ===================================

// Definições de pinos
#define DHTPIN 15          // Pino do sensor DHT22
#define DHTTYPE DHT22      // Tipo do sensor
#define MOSFET_PIN 25      // Pino de controle do MOSFET (ou Relé)

// Configurações do sistema
#define UMIDADE_MIN 60.0   // Umidade mínima desejada (%) - AJUSTE AQUI!
#define TEMPO_LEITURA 2000 // Intervalo entre leituras (ms)

// Inicializa o sensor DHT
DHT dht(DHTPIN, DHTTYPE);

// Variáveis globais
bool umidificadorLigado = false;

void setup() {
  // Inicializa comunicação serial
  Serial.begin(115200);
  Serial.println("=== Sistema de Controle de Umidade ===");
  Serial.println("Inicializando...\n");
  
  // Configura pino do MOSFET como saída
  pinMode(MOSFET_PIN, OUTPUT);
  digitalWrite(MOSFET_PIN, LOW);
  
  // Inicializa sensor DHT22
  dht.begin();
  
  delay(2000); // Aguarda estabilização do sensor
  Serial.println("Sistema pronto!\n");
}

void loop() {
  // Lê os dados do sensor
  float umidade = dht.readHumidity();
  float temperatura = dht.readTemperature();
  
  // Verifica se a leitura foi bem-sucedida
  if (isnan(umidade) || isnan(temperatura)) {
    Serial.println("Erro ao ler o sensor DHT22!");
    delay(TEMPO_LEITURA);
    return;
  }
  
  // Exibe leituras no monitor serial
  Serial.println("------------------------");
  Serial.print("Temperatura: ");
  Serial.print(temperatura);
  Serial.println(" °C");
  
  Serial.print("Umidade: ");
  Serial.print(umidade);
  Serial.println(" %");
  
  // Lógica de controle do umidificador
  if (umidade < UMIDADE_MIN) {
    // Umidade baixa - LIGA o umidificador
    if (!umidificadorLigado) {
      digitalWrite(MOSFET_PIN, HIGH);
      umidificadorLigado = true;
      Serial.println(">> UMIDIFICADOR LIGADO <<");
      Serial.println("Umidade abaixo do limite!");
    } else {
      Serial.println("Status: Umidificador ativo");
    }
  } else {
    // Umidade adequada - DESLIGA o umidificador
    if (umidificadorLigado) {
      digitalWrite(MOSFET_PIN, LOW);
      umidificadorLigado = false;
      Serial.println(">> UMIDIFICADOR DESLIGADO <<");
      Serial.println("Umidade normalizada!");
    } else {
      Serial.println("Status: Umidade OK");
    }
  }
  
  Serial.println("------------------------\n");
  
  // Aguarda antes da próxima leitura
  delay(TEMPO_LEITURA);
}
